// Digital circuit INC.dig as structural Verilog
module INC (
  input  in_1,
  input  clk,
  input  in_5,
  output [7:0] out_2,
  output out_4,
  output [7:0] out_6
);

  wire and_1_out, fsm2_1_p1, fsm2_1_p2, fsm2_1_p6, fsm2_1_p7, fsm2_1_p8, not_1_out, or_1_out, or_2_out;
  wire [2:0] add_2_s, cnt8_2_0_q, multiplexer_2_out;
  wire [3:0] add_1_s, cnt16_4_0_q, multiplexer_1_out;
  wire [7:0] add_3_s, demultiplexer_1_out_0, multiplexer_3_out, multiplexer_4_out;

  // FSM2 fsm2_1: pin names not known; wires that end beside it: fsm2_1_p1, fsm2_1_p2, in_1, clk, in_5, fsm2_1_p6, fsm2_1_p7, fsm2_1_p8, out_4
  or or_1 (or_1_out, in_5, fsm2_1_p8);
  Multiplexer #(.Bits(4)) multiplexer_1 (.sel(fsm2_1_p7), .in_0(4'b1111), .in_1(add_1_s), .out(multiplexer_1_out));
  Multiplexer #(.Bits(3)) multiplexer_2 (.sel(in_5), .in_0(add_2_s), .in_1(3'b111), .out(multiplexer_2_out));
  Register #(.Bits(4)) cnt16_4_0 (.D(multiplexer_1_out), .C(clk), .en(1'b1), .Q(cnt16_4_0_q));
  Register #(.Bits(3), .isProgramCounter("true")) cnt8_2_0 (
    .D(multiplexer_2_out), .C(clk), .en(or_1_out), .Q(cnt8_2_0_q));
  or or_2 (or_2_out, in_5, out_4);
  not not_1 (not_1_out, or_2_out);
  Add #(.Bits(4)) add_1 (.a(4'b0000), .b(cnt16_4_0_q), .c_i(1'b1), .s(add_1_s));  // open: c_o
  Add #(.Bits(3)) add_2 (.a(3'b000), .b(cnt8_2_0_q), .c_i(1'b1), .s(add_2_s));  // open: c_o
  Demultiplexer #(.Selector_Bits(3)) demultiplexer_1 (
    .sel(add_2_s), .in(in_1), .out_0(demultiplexer_1_out_0[0]), .out_1(demultiplexer_1_out_0[1]),
    .out_2(demultiplexer_1_out_0[2]), .out_3(demultiplexer_1_out_0[3]), .out_4(demultiplexer_1_out_0[4]),
    .out_5(demultiplexer_1_out_0[5]), .out_6(demultiplexer_1_out_0[6]), .out_7(demultiplexer_1_out_0[7]));
  Comparator #(.Bits(4)) comparator_1 (.a(add_1_s), .b(4'b1111), .eq(fsm2_1_p1));  // open: gt, lt
  Comparator #(.Bits(3)) comparator_2 (.a(add_2_s), .b(3'b111), .eq(fsm2_1_p2));  // open: gt, lt
  Multiplexer #(.Bits(8)) multiplexer_3 (.sel(not_1_out), .in_0({8{1'b0}}), .in_1(out_2), .out(multiplexer_3_out));
  and and_1 (and_1_out, not_1_out, fsm2_1_p6);
  Multiplexer #(.Bits(8)) multiplexer_4 (
    .sel(and_1_out), .in_0({8{1'b0}}), .in_1(demultiplexer_1_out_0), .out(multiplexer_4_out));
  Add #(.Bits(8)) add_3 (.a(multiplexer_3_out), .b(multiplexer_4_out), .c_i(1'b0), .s(add_3_s));  // open: c_o
  Register #(.Bits(8)) register_1 (.D(add_3_s), .C(clk), .en(1'b1), .Q(out_2));
  Register #(.Bits(8), .isProgramCounter("true")) register_2 (.D(out_2), .C(clk), .en(out_4), .Q(out_6));

  // Other names for the same wires on the sheet: RST = in_5

  // Notes on the sheet:
  //   in_1: default 1
  //   clk: Hz: 16
  //   CLK
  //   RST
  //   DIN
  //   CNT16\_BIT
  //   CNT8
  //   FSM
  //   BIT\_VLD
  //   CNT16\_E
  //   CNT8\_E
  //   DOUT\_VLD
  //   D\_OUT
  //   LAST\_BIT
endmodule
