// Digital circuit s.dig as structural Verilog
module s (
  input  CNT16,
  input  CNT8,
  input  DIN,
  input  D__VLD_2,
  input  set,
  input  C,
  output CNT16__E,
  output CNT8__E,
  output D__VLD
);

  wire and_1_out, and_2_out, and_3_out, and_4_out, and_5_out, and_6_out, and_7_out, and_8_out, and_9_out,
       and_10_out, and_11_out, not_1_out, not_2_out, not_3_out, not_4_out, not_5_out, not_6_out, not_7_out,
       or_1_out, or_2_out, or_3_out, Z_0_n, Z_1_n, Z_2_n;

  // s s_1: pin names not known
  not not_1 (not_1_out, CNT16);
  not not_2 (not_2_out, CNT8);
  not not_3 (not_3_out, DIN);
  not not_4 (not_4_out, set);
  not not_5 (not_5_out, Z_2_n);
  not not_6 (not_6_out, Z_1_n);
  not not_7 (not_7_out, Z_0_n);
  and and_1 (and_1_out, not_2_out, Z_0_n, Z_2_n);
  and and_2 (and_2_out, not_3_out, not_7_out, not_6_out, not_5_out);
  and and_3 (and_3_out, D__VLD_2, not_7_out, Z_2_n);
  and and_4 (and_4_out, not_7_out, Z_2_n, not_4_out);
  and and_5 (and_5_out, Z_0_n, Z_1_n);
  and and_6 (and_6_out, CNT16, Z_0_n, not_6_out, not_5_out);
  and and_7 (and_7_out, CNT8, not_7_out, Z_1_n);
  and and_8 (and_8_out, not_1_out, Z_0_n, not_6_out);
  and and_9 (and_9_out, not_3_out, not_7_out, not_5_out);
  and and_10 (and_10_out, not_7_out, Z_1_n);
  and and_11 (and_11_out, Z_0_n, Z_2_n);
  and and_12 (CNT16__E, not_1_out, Z_0_n, not_6_out, not_5_out);
  and and_13 (CNT8__E, not_2_out, Z_0_n, Z_2_n);
  and and_14 (D__VLD, Z_0_n, Z_1_n);
  or or_1 (or_1_out, and_6_out, and_7_out);
  or or_2 (or_2_out, and_1_out, and_2_out, and_3_out, and_4_out, and_5_out);
  or or_3 (or_3_out, and_8_out, and_9_out, and_10_out, and_11_out);
  D_FF u_Z_2_n (.D(or_2_out), .C(C), .Q(Z_2_n));  // open: nQ
  D_FF u_Z_1_n (.D(or_1_out), .C(C), .Q(Z_1_n));  // open: nQ
  D_FF u_Z_0_n (.D(or_3_out), .C(C), .Q(Z_0_n));  // open: nQ
  // Probe fsm.fsm on {Z_2_n, Z_1_n, Z_0_n}

  // Notes on the sheet:
  //   C: Hz: 2
endmodule
